# Fritzing sketch wiring (saved by Fritzing 0.9.3b)
breadboards: 1

parts:
  Q2 = TRANSISTOR_NPN [package=to-92]
  S1 = Round Pushbutton
  S2 = Toggle Switch [package=THT]
  U1 = LIPO-1000mAh [package=lipo-1000]
  LED1 = LED - 3mm [color="Red (633nm)" package="3 mm [THT]"]
  R1 = Resistor [tolerance=±5% resistance=1k package="0402 [SMD]"]

nets:
  N1: Q2.E, S2.COM
  N2: Q2.B, R1.Pin_1
  N3: S1.leg1, U1.-, LED1.cathode
  N4: S2.L2, U1.+
